// Logisim project ppu.circ as structural Verilog: 1 circuit, main circuit main
module main (
);

  wire and_1_out, and_2_out, C1_A, C1_B, C1_C, C1_D, C2_A, C2_B, C2_C, C2_D, C3_A, C3_B, C3_C, C3_D,
       clock_1_out, comparator_1_eq, comparator_2_eq, comparator_3_eq, comparator_4_eq, comparator_5_eq,
       comparator_6_eq, comparator_7_eq, comparator_8_eq, comparator_9_eq, comparator_10_eq, d_ff_1_q,
       d_ff_2_q, d_ff_3_q, n7430_2_pin2, n7430_2_pin4, n74161_1_pin1, n74161_1_pin2, n74161_1_pin7,
       n74161_1_pin9, n74161_1_pin10, n74161_2_pin1, n74161_2_pin2, n74161_2_pin7, n74161_2_pin9,
       n74161_2_pin10, n74161_3_pin1, n74161_3_pin2, n74161_3_pin7, n74161_3_pin9, n74161_3_pin10, or_1_out;
  wire [11:0] counter_1_q, counter_2_q;

  Clock clock_1 (.out(clock_1_out));
  Counter #(.max('hfff), .width(12)) counter_1 (
    .clr(comparator_1_eq), .count(clock_1_out), .clk(clock_1_out), .Q(counter_1_q));  // open: load, up, D, carry
  _74161 #(.ShowInternalStructure("true")) u_74161_1 (
    .pin1(n74161_1_pin1), .pin2(n74161_1_pin2), .pin7(n74161_1_pin7), .pin14(C3_A), .pin13(C3_B),
    .pin12(C3_C), .pin11(C3_D), .pin10(n74161_1_pin10), .pin9(n74161_1_pin9));  // open: pin3, pin4, pin5, pin6, pin15
  _74161 #(.ShowInternalStructure("true")) u_74161_2 (
    .pin1(n74161_2_pin1), .pin2(n74161_2_pin2), .pin7(n74161_2_pin7), .pin15(n74161_1_pin2), .pin14(C2_A),
    .pin13(C2_B), .pin12(C2_C), .pin11(C2_D), .pin10(n74161_2_pin10), .pin9(n74161_2_pin9));  // open: pin3, pin4, pin5, pin6
  _74161 #(.ShowInternalStructure("true")) u_74161_3 (
    .pin1(n74161_3_pin1), .pin2(n74161_3_pin2), .pin7(n74161_3_pin7), .pin15(n74161_2_pin2), .pin14(C1_A),
    .pin13(C1_B), .pin12(C1_C), .pin11(C1_D), .pin10(n74161_3_pin10), .pin9(n74161_3_pin9));  // open: pin3, pin4, pin5, pin6
  Clock clock_2 (.out(n74161_3_pin2));
  Comparator #(.width(12)) comparator_1 (.a(12'h2fa), .b(counter_1_q), .eq(comparator_1_eq));  // open: gt, lt
  Comparator #(.width(12)) comparator_2 (.a({12{1'b0}}), .b(counter_1_q), .eq(comparator_2_eq));  // open: gt, lt
  Comparator #(.width(12)) comparator_3 (.a(12'h5b), .b(counter_1_q), .eq(comparator_3_eq));  // open: gt, lt
  Comparator #(.width(12)) comparator_4 (.a(12'h5c), .b(counter_1_q), .eq(comparator_4_eq));  // open: gt, lt
  Comparator #(.width(12)) comparator_5 (.a(12'h89), .b(counter_1_q), .eq(comparator_5_eq));  // open: gt, lt
  _7430 #(.ShowInternalStructure("true")) u_7430_1 ();  // open: pin1, pin2, pin3, pin4, pin5, pin6, pin13, pin12, pin11, pin10, pin9, pin8
  _7430 #(.ShowInternalStructure("true")) u_7430_2 (
    .pin2(n7430_2_pin2), .pin4(n7430_2_pin4), .pin5(C2_A), .pin6(C2_B), .pin12(C2_C), .pin11(C2_D));  // open: pin1, pin3, pin13, pin10, pin9, pin8
  _7421 #(.ShowInternalStructure("true")) u_7421_1 (
    .pin1(C1_A), .pin2(C1_B), .pin4(C1_C), .pin5(C1_D));  // open: pin3, pin6, pin13, pin12, pin11, pin10, pin9, pin8
  // Probe on and_1_out
  and and_1 (and_1_out, comparator_5_eq, d_ff_3_q);
  D_Flip_Flop d_ff_1 (.Q(d_ff_1_q), .preset(comparator_3_eq), .reset(comparator_2_eq));  // open: D, clk, Qn
  // Probe on d_ff_1_q
  Counter #(.max('hfff), .width(12)) counter_2 (
    .clr(comparator_6_eq), .count(comparator_1_eq), .clk(comparator_1_eq), .Q(counter_2_q));  // open: load, up, D, carry
  // Probe on and_2_out
  and and_2 (and_2_out, comparator_4_eq, d_ff_3_q);
  Comparator #(.width(12)) comparator_6 (.a(12'h20c), .b(counter_2_q), .eq(comparator_6_eq));  // open: gt, lt
  Comparator #(.width(12)) comparator_7 (.a(12'h1eb), .b(counter_2_q), .eq(comparator_7_eq));  // open: gt, lt
  Comparator #(.width(12)) comparator_8 (.a(12'h1ed), .b(counter_2_q), .eq(comparator_8_eq));  // open: gt, lt
  Comparator #(.width(12)) comparator_9 (.a({12{1'b0}}), .b(counter_2_q), .eq(comparator_9_eq));  // open: gt, lt
  Comparator #(.width(12)) comparator_10 (.a(12'h1e0), .b(counter_2_q), .eq(comparator_10_eq));  // open: gt, lt
  or or_1 (or_1_out, comparator_8_eq, comparator_9_eq);
  D_Flip_Flop d_ff_2 (.Q(d_ff_2_q), .preset(or_1_out), .reset(comparator_7_eq));  // open: D, clk, Qn
  // Probe on d_ff_2_q
  D_Flip_Flop d_ff_3 (.Q(d_ff_3_q), .preset(comparator_9_eq), .reset(comparator_10_eq));  // open: D, clk, Qn
  // also tied to VCC on the sheet: {n74161_1_pin1, n74161_2_pin1, n74161_3_pin1, n74161_1_pin10, n74161_1_pin7, n74161_2_pin10, n74161_2_pin7, n74161_3_pin10, n74161_3_pin7, n74161_1_pin9, n74161_2_pin9, n74161_3_pin9}
endmodule
